// Logisim project jrmips.circ as structural Verilog: 21 circuits, main circuit main
module main (
);

  wire alu_container_1_load_en, alu_container_1_store_en, Clock_out, decoder_container_1_cpu_en,
       decoder_container_1_sys_op, decoder_container_1_word_op, or_1_out;
  wire [1:0] decoder_container_1_type_en;
  wire [2:0] decoder_container_1_alu_op, decoder_container_1_br_op;
  wire [3:0] decoder_container_1_shamt_out;
  wire [7:0] adder_1_out, alu_container_1_address_out, alu_container_1_pc_out, decoder_container_1_pc_out,
       decoder_container_1_pc_out_br, decoder_container_1_uns_imm_out, register_1_q;
  wire [15:0] alu_container_1_alu_out, alu_container_1_branch_out, alu_container_1_display_out,
       alu_container_1_word_out, decoder_container_1_rs_out, decoder_container_1_rt_out, multiplexer_1_out,
       ram_1_data, rom_1_data;

  Register register_1 (
    .D(decoder_container_1_pc_out), .en(decoder_container_1_cpu_en), .Q(register_1_q), .clk(Clock_out));  // open: clr
  LED led_1 (.in(decoder_container_1_cpu_en));
  LED led_2 (.in(decoder_container_1_cpu_en));
  LED led_3 (.in(decoder_container_1_cpu_en));
  Clock Clock (.out(Clock_out));
  Adder adder_1 (.a(8'h1), .b(register_1_q), .out(adder_1_out));  // open: cin, cout
  ROM #(.dataWidth(16)) rom_1 (.addr(register_1_q), .data(rom_1_data), .sel(1'b1));
  Decoder_Container decoder_container_1 (
    .PC_out(decoder_container_1_pc_out), .PC_in(adder_1_out), .instruction(rom_1_data),
    .write_reg(multiplexer_1_out), .type_en(decoder_container_1_type_en),
    .ALU_op(decoder_container_1_alu_op), .br_op(decoder_container_1_br_op),
    .word_op(decoder_container_1_word_op), .sys_op(decoder_container_1_sys_op),
    .CPU_en(decoder_container_1_cpu_en), .Clock(Clock_out), .PC_in_br(alu_container_1_pc_out),
    .PC_out_br(decoder_container_1_pc_out_br), .rs_out(decoder_container_1_rs_out),
    .rt_out(decoder_container_1_rt_out), .uns_imm_out(decoder_container_1_uns_imm_out),
    .shamt_out(decoder_container_1_shamt_out));
  ALU_Container alu_container_1 (
    .PC_in(decoder_container_1_pc_out_br), .rs_in(decoder_container_1_rs_out),
    .rt_in(decoder_container_1_rt_out), .imm(decoder_container_1_uns_imm_out),
    .shamt_in(decoder_container_1_shamt_out), .Branch_op(decoder_container_1_br_op),
    .sys_op(decoder_container_1_sys_op), .ALU_op(decoder_container_1_alu_op),
    .Word_op(decoder_container_1_word_op), .Type_en(decoder_container_1_type_en), .Clock(Clock_out),
    .Display_out(alu_container_1_display_out), .PC_out(alu_container_1_pc_out),
    .branch_out(alu_container_1_branch_out), .ALU_out(alu_container_1_alu_out),
    .address_out(alu_container_1_address_out), .Word_out(alu_container_1_word_out),
    .store_en(alu_container_1_store_en), .load_en(alu_container_1_load_en));
  Hex_Digit_Display hex_digit_display_1 (.value(alu_container_1_display_out[15:12]), .dp(1'b0));
  Hex_Digit_Display hex_digit_display_2 (.value(alu_container_1_display_out[11:8]), .dp(1'b0));
  or or_1 (or_1_out, alu_container_1_load_en, alu_container_1_store_en);
  Hex_Digit_Display hex_digit_display_3 (.value(alu_container_1_display_out[7:4]), .dp(1'b0));
  Hex_Digit_Display hex_digit_display_4 (.value(alu_container_1_display_out[3:0]), .dp(1'b0));
  Multiplexer #(.select(2), .width(16), .enable("false")) multiplexer_1 (
    .in0(alu_container_1_alu_out), .in1(alu_container_1_branch_out), .in2(ram_1_data),
    .out(multiplexer_1_out), .sel(decoder_container_1_type_en));  // open: in3
  RAM #(.dataWidth(16), .bus("separate")) ram_1 (
    .addr(alu_container_1_address_out), .din(alu_container_1_word_out), .data(ram_1_data),
    .str(alu_container_1_store_en), .sel(or_1_out), .clk(Clock_out), .ld(alu_container_1_load_en));  // open: clr

  // Notes on the sheet:
  //   Brandon S. Hang
  //   Project 2 - JrMIPS
  //   bsh41@pitt.edu
  //   v2.538
  //   contents of rom_1 (hex, n*v repeats v):
  //   1fc1 2fff 1901 29ff 800 1001 2013 bc18 1901 2955 800 f000 2ffe 7dc1 0 9024 21fe bc18 7dc0 2e02 ac00
endmodule

module ALU (
  input  [2:0] Opcode,
  input  [15:0] rs_in,
  input  [15:0] rt_in,
  input  [3:0] shamt,
  output [15:0] rs_out
);

  wire [15:0] adder_1_out, and_1_out, nor_1_out, shifter_1_out, shifter_2_out, subtractor_1_out;

  Adder #(.width(16)) adder_1 (.a(rs_in), .b(rt_in), .out(adder_1_out));  // open: cin, cout
  Subtractor #(.width(16)) subtractor_1 (.a(rs_in), .b(rt_in), .out(subtractor_1_out));  // open: bin, bout
  assign and_1_out = rs_in & rt_in;  // AND_Gate and_1, 16 bits wide
  assign nor_1_out = ~(rs_in | rt_in);  // NOR_Gate nor_1, 16 bits wide
  Shifter #(.width(16)) shifter_1 (.in(rs_in), .\dist (shamt), .out(shifter_1_out));
  Shifter #(.width(16), .shift("lr")) shifter_2 (.in(rs_in), .\dist (shamt), .out(shifter_2_out));
  Multiplexer #(.select(3), .width(16), .enable("false")) multiplexer_1 (
    .in0(adder_1_out), .in1(subtractor_1_out), .in2(and_1_out), .in3(nor_1_out), .in4(shifter_1_out),
    .in5(shifter_2_out), .out(rs_out), .sel(Opcode));  // open: in6, in7
endmodule

module Branch (
  input  [2:0] br_op,
  input  [7:0] PC_in,
  input  [15:0] rs,
  input  [7:0] imm,
  output [7:0] PC_out,
  output [15:0] \output 
);

  wire br_ctrl2_1_bx_bz_dmx0, br_ctrl2_1_bx_bz_dmx_combo, br_ctrl2_1_jal_buff0, bx_1_not_equal_0,
       bz_1_equal_0, multiplexer_1_out;
  wire [7:0] bit_extender_1_out, controlled_buffer_1_out, multiplexer_2_out;
  wire [15:0] demultiplexer_1_out0, demultiplexer_1_out1;

  Demultiplexer #(.width(16), .enable("false")) demultiplexer_1 (
    .out0(demultiplexer_1_out0), .out1(demultiplexer_1_out1), .in(rs), .sel(br_ctrl2_1_bx_bz_dmx_combo));
  Br_Ctrl2 br_ctrl2_1 (
    .br_op2(br_op[2]), .br_op1(br_op[1]), .br_op0(br_op[0]), .bx_bz_dmx_combo(br_ctrl2_1_bx_bz_dmx_combo),
    .bx_bz_dmx0(br_ctrl2_1_bx_bz_dmx0), .jal_buff0(br_ctrl2_1_jal_buff0));
  Bit_Extender #(.in_width(16), .out_width(8)) bit_extender_1 (.in(demultiplexer_1_out0), .out(bit_extender_1_out));
  bx bx_1 (.rs(demultiplexer_1_out1), .not_equal_0(bx_1_not_equal_0));
  bz bz_1 (.rs(demultiplexer_1_out1), .equal_0(bz_1_equal_0));
  Adder adder_1 (.b(8'h1));  // open: a, out, cin, cout
  assign controlled_buffer_1_out = br_ctrl2_1_jal_buff0 ? PC_in : 8'bz;  // Controlled_Buffer controlled_buffer_1
  Multiplexer #(.disabled(0), .enable("false")) multiplexer_1 (
    .in0(bx_1_not_equal_0), .in1(bz_1_equal_0), .out(multiplexer_1_out), .sel(br_ctrl2_1_bx_bz_dmx0));
  assign \output  = {{8{1'b0}}, controlled_buffer_1_out};  // Bit_Extender bit_extender_2
  Multiplexer #(.width(8), .disabled(0), .enable("false")) multiplexer_2 (
    .in0(PC_in), .in1(imm), .out(multiplexer_2_out), .sel(multiplexer_1_out));
  Multiplexer #(.select(3), .width(8), .enable("false")) multiplexer_3 (
    .in0(multiplexer_2_out), .in1(multiplexer_2_out), .in2(bit_extender_1_out), .in3(imm), .in4(imm),
    .out(PC_out), .sel(br_op));  // open: in5, in6, in7
endmodule

module Word (
  input  word_op,
  input  [1:0] type_en,
  input  [15:0] rs_data,
  input  [15:0] rt_data,
  output Store_en,
  output Load_en,
  output [15:0] data_out,
  output [7:0] address_out
);

  wire and_1_out, not_1_out, not_2_out;

  not not_1 (not_1_out, type_en[0]);
  and and_1 (and_1_out, type_en[1], not_1_out);
  not not_2 (not_2_out, word_op);
  Bit_Extender #(.in_width(16), .out_width(8)) bit_extender_1 (.in(rt_data), .out(address_out));
  and str (Store_en, and_1_out, word_op);
  and ld (Load_en, and_1_out, not_2_out);
  assign data_out = Store_en ? rs_data : 16'bz;  // Controlled_Buffer controlled_buffer_1
endmodule

// Disp
module Display (
  input  Clock,
  input  Sys_select,
  input  [15:0] rs_in,
  input  [1:0] Type_in,
  output [15:0] to_display
);

  wire and_1_out, display_ctrl_1_output_0, not_1_out;

  Display_Ctrl display_ctrl_1 (
    .Sys_0(Sys_select), .Type_1(Type_in[1]), .Type_0(Type_in[0]), .Output_0(display_ctrl_1_output_0));
  not not_1 (not_1_out, Clock);
  and and_1 (and_1_out, not_1_out, display_ctrl_1_output_0);
  Register #(.width(16)) register_1 (.D(rs_in), .en(1'b1), .Q(to_display), .clk(and_1_out));  // open: clr
endmodule

// Reg
module Registers (
  input  [2:0] rs_control,
  input  [2:0] rt_control,
  input  [15:0] WriteRegister,
  input  write_en,
  input  Clock,
  output [15:0] rs_out,
  output [15:0] rt_out
);

  wire decoder_1_out0, decoder_1_out1, decoder_1_out2, decoder_1_out3, decoder_1_out4, decoder_1_out5,
       decoder_1_out6, decoder_1_out7;
  wire [15:0] demultiplexer_1_out0, demultiplexer_1_out1, demultiplexer_1_out2, demultiplexer_1_out3,
       demultiplexer_1_out4, demultiplexer_1_out5, demultiplexer_1_out6, demultiplexer_1_out7, r0_q, r1_q,
       r2_q, r3_q, r4_q, r5_q, r6_q, r7_q;

  Demultiplexer #(.select(3), .width(16), .disabled(0)) demultiplexer_1 (
    .out0(demultiplexer_1_out0), .out1(demultiplexer_1_out1), .out2(demultiplexer_1_out2),
    .out3(demultiplexer_1_out3), .out4(demultiplexer_1_out4), .out5(demultiplexer_1_out5),
    .out6(demultiplexer_1_out6), .out7(demultiplexer_1_out7), .in(WriteRegister), .sel(rs_control),
    .en(write_en));
  Decoder_part #(.select(3), .disabled(0)) decoder_1 (
    .out0(decoder_1_out0), .out1(decoder_1_out1), .out2(decoder_1_out2), .out3(decoder_1_out3),
    .out4(decoder_1_out4), .out5(decoder_1_out5), .out6(decoder_1_out6), .out7(decoder_1_out7),
    .sel(rs_control), .en(write_en));
  Register #(.width(16)) r0 (.D(demultiplexer_1_out0), .en(decoder_1_out0), .Q(r0_q), .clk(Clock));  // open: clr
  Register #(.width(16)) r1 (.D(demultiplexer_1_out1), .en(decoder_1_out1), .Q(r1_q), .clk(Clock));  // open: clr
  Register #(.width(16)) r2 (.D(demultiplexer_1_out2), .en(decoder_1_out2), .Q(r2_q), .clk(Clock));  // open: clr
  Register #(.width(16)) r3 (.D(demultiplexer_1_out3), .en(decoder_1_out3), .Q(r3_q), .clk(Clock));  // open: clr
  Register #(.width(16)) r4 (.D(demultiplexer_1_out4), .en(decoder_1_out4), .Q(r4_q), .clk(Clock));  // open: clr
  Register #(.width(16)) r5 (.D(demultiplexer_1_out5), .en(decoder_1_out5), .Q(r5_q), .clk(Clock));  // open: clr
  Register #(.width(16)) r6 (.D(demultiplexer_1_out6), .en(decoder_1_out6), .Q(r6_q), .clk(Clock));  // open: clr
  Register #(.width(16)) r7 (.D(demultiplexer_1_out7), .en(decoder_1_out7), .Q(r7_q), .clk(Clock));  // open: clr
  Multiplexer #(.select(3), .width(16), .enable("false")) multiplexer_1 (
    .in0(r0_q), .in1(r1_q), .in2(r2_q), .in3(r3_q), .in4(r4_q), .in5(r5_q), .in6(r6_q), .in7(r7_q),
    .out(rs_out), .sel(rs_control));
  Multiplexer #(.select(3), .width(16), .enable("false")) multiplexer_2 (
    .in0(r0_q), .in1(r1_q), .in2(r2_q), .in3(r3_q), .in4(r4_q), .in5(r5_q), .in6(r6_q), .in7(r7_q),
    .out(rt_out), .sel(rt_control));
endmodule

// Sign
module Sign_Extender (
  input  [7:0] imm_in,
  input  b0_Subop,
  output [15:0] imm_out
);

  wire [15:0] bit_extender_1_out, bit_extender_2_out;

  assign bit_extender_1_out = {{8{imm_in[7]}}, imm_in};  // Bit_Extender bit_extender_1
  Multiplexer #(.width(16), .enable("false")) multiplexer_1 (
    .in0(bit_extender_1_out), .in1(bit_extender_2_out), .out(imm_out), .sel(b0_Subop));
  assign bit_extender_2_out = {{8{1'b0}}, imm_in};  // Bit_Extender bit_extender_2
endmodule

module Fetch (
  input  [15:0] instr_in,
  output [1:0] Type_00,
  output Format_0,
  output [2:0] rs_read,
  output [2:0] rt_read,
  output [7:0] imm
);

  wire and_1_out, and_2_out, and_3_out, and_4_out, and_5_out, and_6_out, not_1_out, not_2_out, not_3_out,
       not_4_out, not_5_out, not_6_out, not_7_out, not_8_out, not_9_out, not_10_out, not_11_out;

  not not_1 (not_1_out, instr_in[15]);
  not not_2 (not_2_out, instr_in[14]);
  not not_3 (not_3_out, instr_in[13]);
  not not_4 (not_4_out, instr_in[12]);
  and and_1 (and_1_out, instr_in[14], instr_in[13]);
  not not_5 (not_5_out, instr_in[14]);
  not not_6 (not_6_out, instr_in[13]);
  not not_7 (not_7_out, instr_in[12]);
  not not_8 (not_8_out, instr_in[15]);
  not not_9 (not_9_out, instr_in[12]);
  not not_10 (not_10_out, instr_in[13]);
  not not_11 (not_11_out, instr_in[14]);
  and and_2 (and_2_out, not_1_out, not_2_out, not_3_out, not_4_out);
  and and_3 (and_3_out, not_5_out, not_6_out, not_7_out);
  and and_4 (and_4_out, not_8_out, instr_in[13], not_9_out);
  or or_1 (Format_0, and_4_out, and_5_out, and_6_out);
  and and_5 (and_5_out, instr_in[15], not_10_out);
  and and_6 (and_6_out, instr_in[15], not_11_out, instr_in[12]);
  or or_2 (Type_00[1], and_2_out, and_1_out);
  or or_3 (Type_00[0], and_3_out, instr_in[15]);

  assign imm = instr_in[8:1];
  assign rs_read = instr_in[11:9];
  assign rt_read = instr_in[8:6];
endmodule

module Decoder (
  input  [15:0] instr_in,
  input  [1:0] Type_ctrl,
  output [2:0] ALU_select,
  output Subop,
  output [2:0] Br_select,
  output Word_select,
  output Sys_select,
  output CPU_en
);

  wire [15:0] demultiplexer_1_out0, demultiplexer_1_out1, demultiplexer_1_out2, demultiplexer_1_out3;

  Demultiplexer #(.select(2), .width(16), .disabled(0), .enable("false")) demultiplexer_1 (
    .out0(demultiplexer_1_out0), .out1(demultiplexer_1_out1), .out2(demultiplexer_1_out2),
    .out3(demultiplexer_1_out3), .in(instr_in), .sel(Type_ctrl));
  ALU_Ctrl alu_ctrl_1 (
    .instr_in(demultiplexer_1_out0), .ALU_2(ALU_select[2]), .ALU_1(ALU_select[1]), .ALU_0(ALU_select[0]),
    .Subop(Subop));
  Br_Ctrl br_ctrl_1 (
    .instr_in(demultiplexer_1_out1), .branch_2(Br_select[2]), .branch_1(Br_select[1]), .branch_0(Br_select[0]));
  Word_Ctrl word_ctrl_1 (.instr_in(demultiplexer_1_out2), .word_0(Word_select));
  Sys_Ctrl sys_ctrl_1 (.instr_in(demultiplexer_1_out3), .Sys_0(Sys_select));
  not not_1 (CPU_en, Sys_select);
endmodule

module bx (
  input  [15:0] rs,
  output not_equal_0
);

  Comparator #(.width(16), .mode("unsigned")) comparator_1 (.a(rs), .b({16{1'b0}}), .gt(not_equal_0));  // open: eq, lt
endmodule

module bz (
  input  [15:0] rs,
  output equal_0
);

  Comparator #(.width(16), .mode("unsigned")) comparator_1 (.a(rs), .b({16{1'b0}}), .eq(equal_0));  // open: gt, lt
endmodule

// AL_c
module ALU_Ctrl (
  input  [15:0] instr_in,
  output ALU_2,
  output ALU_1,
  output ALU_0,
  output Subop
);

  wire and_2_out, and_3_out, not_1_out;

  and and_1 (ALU_1, instr_in[13], instr_in[12]);
  not not_1 (not_1_out, instr_in[13]);
  and and_2 (and_2_out, not_1_out, instr_in[0]);
  or or_1 (ALU_0, and_2_out, and_3_out);
  and and_3 (and_3_out, instr_in[12], instr_in[0]);

  assign ALU_2 = instr_in[14];
  assign Subop = instr_in[0];
endmodule

// Br_c
module Br_Ctrl (
  input  [15:0] instr_in,
  output branch_2,
  output branch_1,
  output branch_0
);


  assign branch_0 = instr_in[12];
  assign branch_1 = instr_in[13];
  assign branch_2 = instr_in[14];
endmodule

// ctrl
module Br_Ctrl2 (
  input  br_op2,
  input  br_op1,
  input  br_op0,
  output bx_bz_dmx_combo,
  output bx_bz_dmx0,
  output jal_buff0
);

  not not_1 (bx_bz_dmx_combo, br_op1);
  and and_1 (jal_buff0, br_op1, br_op0);

  assign bx_bz_dmx0 = br_op0;
endmodule

// W_c
module Word_Ctrl (
  input  [15:0] instr_in,
  output word_0
);


  assign word_0 = instr_in[0];
endmodule

// S_c
module Sys_Ctrl (
  input  [15:0] instr_in,
  output Sys_0
);


  assign Sys_0 = instr_in[15];
endmodule

// PC_c
module PC_Ctrl (
  input  [1:0] type_in,
  output PC_bypass
);

  wire not_1_out;

  not not_1 (not_1_out, type_in[1]);
  and and_1 (PC_bypass, not_1_out, type_in[0]);
endmodule

// Dsp_c
module Display_Ctrl (
  input  Sys_0,
  input  Type_1,
  input  Type_0,
  output Output_0
);

  wire not_1_out;

  not not_1 (not_1_out, Sys_0);
  and and_1 (Output_0, Type_1, Type_0, not_1_out);
endmodule

// PC_b
module PC_bypass (
  input  [7:0] PC_from_br,
  input  [1:0] Type,
  input  [7:0] PC_in,
  output [7:0] PC_out,
  output [7:0] PC_to_br
);

  wire pc_ctrl_1_pc_bypass;
  wire [7:0] demultiplexer_1_out0;

  Multiplexer #(.width(8), .enable("false")) multiplexer_1 (
    .in0(demultiplexer_1_out0), .in1(PC_from_br), .out(PC_out), .sel(pc_ctrl_1_pc_bypass));
  PC_Ctrl pc_ctrl_1 (.type_in(Type), .PC_bypass(pc_ctrl_1_pc_bypass));
  Demultiplexer #(.width(8), .enable("false")) demultiplexer_1 (
    .out0(demultiplexer_1_out0), .out1(PC_to_br), .in(PC_in), .sel(pc_ctrl_1_pc_bypass));
endmodule

// Ultra_ALU
module ALU_Container (
  input  [2:0] Branch_op,
  input  sys_op,
  input  [2:0] ALU_op,
  input  Word_op,
  input  [1:0] Type_en,
  input  [7:0] PC_in,
  input  [15:0] rs_in,
  input  [15:0] rt_in,
  input  [7:0] imm,
  input  [3:0] shamt_in,
  input  Clock,
  output [15:0] Display_out,
  output [7:0] PC_out,
  output [15:0] branch_out,
  output [15:0] ALU_out,
  output [7:0] address_out,
  output [15:0] Word_out,
  output store_en,
  output load_en
);

  Display display_1 (.Sys_select(sys_op), .rs_in(rs_in), .Type_in(Type_en), .Clock(Clock), .to_display(Display_out));
  Branch branch_1 (.PC_in(PC_in), .rs(rs_in), .imm(imm), .br_op(Branch_op), .PC_out(PC_out), .\output (branch_out));
  ALU alu_1 (.rs_in(rs_in), .rt_in(rt_in), .shamt(shamt_in), .Opcode(ALU_op), .rs_out(ALU_out));
  Word word_1 (
    .rs_data(rs_in), .rt_data(rt_in), .Store_en(store_en), .Load_en(load_en), .data_out(Word_out),
    .address_out(address_out), .word_op(Word_op), .type_en(Type_en));
endmodule

// Decoder
module Decoder_Container (
  input  [7:0] PC_in_br,
  input  [7:0] PC_in,
  input  [15:0] instruction,
  input  [15:0] write_reg,
  input  Clock,
  output [1:0] type_en,
  output [2:0] ALU_op,
  output [2:0] br_op,
  output word_op,
  output sys_op,
  output [7:0] PC_out,
  output [7:0] PC_out_br,
  output [15:0] rs_out,
  output [15:0] rt_out,
  output [7:0] uns_imm_out,
  output [3:0] shamt_out,
  output CPU_en
);

  wire decoder_1_subop, fetch_1_format_0;
  wire [2:0] fetch_1_rs_read, fetch_1_rt_read;
  wire [15:0] registers_1_rt_out, sign_extender_1_imm_out;

  Fetch fetch_1 (
    .instr_in(instruction), .Type_00(type_en), .Format_0(fetch_1_format_0), .rs_read(fetch_1_rs_read),
    .rt_read(fetch_1_rt_read), .imm({uns_imm_out[7:4], shamt_out}));
  PC_bypass pc_bypass_1 (.PC_out(PC_out), .Type(type_en), .PC_in(PC_in), .PC_from_br(PC_in_br), .PC_to_br(PC_out_br));
  Decoder decoder_1 (
    .instr_in(instruction), .Type_ctrl(type_en), .CPU_en(CPU_en), .ALU_select(ALU_op),
    .Subop(decoder_1_subop), .Br_select(br_op), .Word_select(word_op), .Sys_select(sys_op));
  Registers registers_1 (
    .rs_control(fetch_1_rs_read), .rt_control(fetch_1_rt_read), .WriteRegister(write_reg), .write_en(1'b1),
    .Clock(Clock), .rs_out(rs_out), .rt_out(registers_1_rt_out));
  Sign_Extender sign_extender_1 (
    .imm_in({uns_imm_out[7:4], shamt_out}), .b0_Subop(decoder_1_subop), .imm_out(sign_extender_1_imm_out));
  Multiplexer #(.width(16), .enable("false")) multiplexer_1 (
    .in0(registers_1_rt_out), .in1(sign_extender_1_imm_out), .out(rt_out), .sel(fetch_1_format_0));

  assign uns_imm_out[3:0] = shamt_out;
endmodule
